# Fritzing sketch sprinkler controller (saved by Fritzing 0.9.3b)
breadboards: 1

parts:
  Part1 = Adafruit Metro with Headers [part_number="Adafruit #2488"]
  U1 = LCD-16X2 [package=lcd-16x2]  # not connected
  Part2 = Adafruit PCF8523 RTC [part_number="Adafruit #3295"]
  U2 = atmega328 [package=dip]  # not connected
  S1 = Pushbutton [package="[THT]"]
  S2 = Pushbutton [package="[THT]"]
  switch1 = RM-series Subminiature Rotary Switch
  R1 = Resistor [tolerance=±5% resistance=2.2k package=THT]
  R2 = Resistor [tolerance=±5% resistance=220 package=THT]
  R3 = Resistor [tolerance=±5% resistance=470 package=THT]
  R4 = Resistor [tolerance=±5% resistance=680 package=THT]
  R5 = Resistor [tolerance=±5% resistance=1k package=THT]
  R6 = Resistor [tolerance=±5% resistance=2.2k package=THT]
  R7 = Resistor [tolerance=±5% resistance=3.3k package=THT]
  R8 = Resistor [tolerance=±5% resistance=220 package=THT]
  R9 = Resistor [tolerance=±5% resistance=220 package=THT]

nets:
  N1: Part1.AD0, switch1.1, R1.Pin_0, R2.Pin_1
  N2: Part1.AD1, S1.Pin_1, S1.Pin_2, R8.Pin_0
  N3: Part1.AD2, S2.Pin_1, S2.Pin_2, R9.Pin_0
  N4: Part1.AD5/SCL, Part2.SCL
  N5: Part1.AD4/SDA, Part2.SDA
  +5V: Part1.+5V, Part2.VCC, R1.Pin_1, R8.Pin_1, R9.Pin_1
  GND: Part1.GND, Part2.GND, S1.Pin_3, S1.Pin_4, S2.Pin_3, S2.Pin_4, switch1.0
  N6: switch1.2, R2.Pin_0, R3.Pin_0
  N7: switch1.3, R3.Pin_1, R4.Pin_1
  N8: switch1.4, R4.Pin_0, R5.Pin_0
  N9: switch1.5, R5.Pin_1, R6.Pin_1
  N10: switch1.6, R6.Pin_0, R7.Pin_0
  N11: switch1.7, R7.Pin_1

custom parts:
  Adafruit Metro with Headers: We sure love the ATmega328 here at Adafruit, and we use them a lot for our own projects. The processor has plenty of GPIO, Analog inputs, hardware UART SPI and I2C, timers and PWM galore - just enough for most simple projects. When we need to go small, we use a Pro Trinket 3V or 5V, but when size isn't as much of a concern, and an USB-serial converter is required, we reach for an Adafruit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
  Adafruit PCF8523 RTC: This is a great battery-backed real time clock (RTC) that allows your microcontroller project to keep track of time even if it is reprogrammed, or if the power is lost. Perfect for datalogging, clock-building, time stamping, timers and alarms, etc. Equipped with PCF8523 RTC - it can run from 3.3V or 5V power & logic! Works great with an Arduino using our RTC library, with CircuitPython or with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
